// Logisim project dicksingh.circ as structural Verilog: 5 circuits, main circuit main
module main (
  input  [7:0] in_1,
  output [7:0] PC,
  output [15:0] out_3,
  output odd_parity,
  output even_parity,
  output zero,
  output sigh
);

  wire Clock, RESET, shift_register_1_out;
  wire [7:0] accumulator_q, MAR_q, RB_q, RZ_q, undriven;
  wire [11:0] IR_q, MBR_q, rom_1_data;
  wire [15:8] RZ_q_2;

  pc pc_1 (.PC_INput(in_1), .PC_enable(shift_register_1_out), .Clock(Clock), .PC_reset(RESET), .PC_OUT(PC));
  Register MAR (.D(PC), .en(shift_register_1_out), .Q(MAR_q), .clk(Clock), .clr(RESET));
  Shift_Register #(.length(6)) shift_register_1 (
    .in(shift_register_1_out), .clk(Clock), .out(shift_register_1_out));  // open: shift, load, clr, d0, q0, d1, q1, d2, q2, d3, q3, d4, q4, d5, q5
  ROM #(.dataWidth(12)) rom_1 (.addr(MAR_q), .data(rom_1_data));  // open: sel
  Register #(.width(12)) MBR (.D(rom_1_data), .Q(MBR_q), .clk(Clock), .clr(RESET));  // open: en
  Register #(.width(12)) IR (.D(MBR_q), .Q(IR_q), .clk(Clock), .clr(RESET));  // open: en
  Register accumulator (.D(RZ_q), .Q(accumulator_q), .clk(Clock), .clr(RESET));  // open: en
  Register RB (.D(undriven), .Q(RB_q), .clk(Clock), .clr(RESET));  // open: en
  Register #(.width(16)) RZ (.D(out_3), .Q({RZ_q_2, RZ_q}), .clk(Clock), .clr(RESET));  // open: en
  Alu alu_1 (.A(accumulator_q), .B(IR_q[11:4]), .SELECT(IR_q[3:0]), .ALU_output(out_3));
  Button button_1 (.out(RESET));
  Hex_Digit_Display hex_digit_display_1 (.value(out_3[15:12]));  // open: dp
  Hex_Digit_Display hex_digit_display_2 (.value(out_3[11:8]));  // open: dp
  PSW psw_1 (
    .INPUT(out_3), .ODD_PARITY(odd_parity), .EVEN_PARITY(even_parity), .ZERO(zero), .SIGN_BIT(sigh));  // open: OP_2, OP_1, HALF_CARRY
  Hex_Digit_Display hex_digit_display_3 (.value(out_3[3:0]));  // open: dp
  Hex_Digit_Display hex_digit_display_4 (.value(out_3[7:4]));  // open: dp
  Clock u_Clock (.out(Clock));

  // Notes on the sheet:
  //   2 opcode ewhat op
  //   register address
  //   01 immediat value
  //   add #oooo ooo1
  //   Code Memory
  //   contents of rom_1 (hex, n*v repeats v):
  //   1 2 1
  //   RESULT
endmodule

module register (
  input  [7:0] DataIn,
  input  clock,
  input  R_W_prime,
  input  [3:0] Rx,
  output [7:0] Dataout
);

  wire decoder_1_out0, decoder_1_out1, decoder_1_out2, decoder_1_out3, decoder_1_out4, decoder_1_out5,
       decoder_1_out6, decoder_1_out7, decoder_1_out8, decoder_1_out9, decoder_1_out10, decoder_1_out11,
       decoder_1_out12, decoder_1_out13, decoder_1_out14, decoder_1_out15, not_1_out;
  wire [3:0] undriven, undriven_2, undriven_3, undriven_4;
  wire [7:0] R0_q, R1_q, R2_q, R3_q, R4_q, R5_q, R6_q, R7_q, R8_q, R9_q, R10_q, R11_q, R12_q, R13_q, R14_q,
       R15_q;

  Hex_Digit_Display hex_digit_display_1 (.value(undriven));  // open: dp
  Hex_Digit_Display hex_digit_display_2 (.value(DataIn[7:4]));  // open: dp
  Hex_Digit_Display hex_digit_display_3 (.value(DataIn[3:0]));  // open: dp
  Hex_Digit_Display hex_digit_display_4 (.value(undriven_2));  // open: dp
  not not_1 (not_1_out, R_W_prime);
  Decoder #(.select(4), .disabled(0)) decoder_1 (
    .out0(decoder_1_out0), .out1(decoder_1_out1), .out2(decoder_1_out2), .out3(decoder_1_out3),
    .out4(decoder_1_out4), .out5(decoder_1_out5), .out6(decoder_1_out6), .out7(decoder_1_out7),
    .out8(decoder_1_out8), .out9(decoder_1_out9), .out10(decoder_1_out10), .out11(decoder_1_out11),
    .out12(decoder_1_out12), .out13(decoder_1_out13), .out14(decoder_1_out14), .out15(decoder_1_out15),
    .sel(Rx), .en(not_1_out));
  Register R0 (.D(DataIn), .en(decoder_1_out0), .Q(R0_q), .clk(clock));  // open: clr
  Register R1 (.D(DataIn), .en(decoder_1_out1), .Q(R1_q), .clk(clock));  // open: clr
  Register R2 (.D(DataIn), .en(decoder_1_out2), .Q(R2_q), .clk(clock));  // open: clr
  Register R3 (.D(DataIn), .en(decoder_1_out3), .Q(R3_q), .clk(clock));  // open: clr
  Register R4 (.D(DataIn), .en(decoder_1_out4), .Q(R4_q), .clk(clock));  // open: clr
  Register R5 (.D(DataIn), .en(decoder_1_out5), .Q(R5_q), .clk(clock));  // open: clr
  Register R6 (.D(DataIn), .en(decoder_1_out6), .Q(R6_q), .clk(clock));  // open: clr
  Register R7 (.D(DataIn), .en(decoder_1_out7), .Q(R7_q), .clk(clock));  // open: clr
  Register R8 (.D(DataIn), .en(decoder_1_out8), .Q(R8_q), .clk(clock));  // open: clr
  Register R9 (.D(DataIn), .en(decoder_1_out9), .Q(R9_q), .clk(clock));  // open: clr
  Register R10 (.D(DataIn), .en(decoder_1_out10), .Q(R10_q), .clk(clock));  // open: clr
  Register R11 (.D(DataIn), .en(decoder_1_out11), .Q(R11_q), .clk(clock));  // open: clr
  Register R12 (.D(DataIn), .en(decoder_1_out12), .Q(R12_q), .clk(clock));  // open: clr
  Register R13 (.D(DataIn), .en(decoder_1_out13), .Q(R13_q), .clk(clock));  // open: clr
  Register R14 (.D(DataIn), .en(decoder_1_out14), .Q(R14_q), .clk(clock));  // open: clr
  Register R15 (.D(DataIn), .en(decoder_1_out15), .Q(R15_q), .clk(clock));  // open: clr
  Hex_Digit_Display hex_digit_display_5 (.value(Dataout[7:4]));  // open: dp
  Hex_Digit_Display hex_digit_display_6 (.value(undriven_3));  // open: dp
  Multiplexer #(.select(4), .width(8)) multiplexer_1 (
    .in0(R0_q), .in1(R1_q), .in2(R2_q), .in3(R3_q), .in4(R4_q), .in5(R5_q), .in6(R6_q), .in7(R7_q),
    .in8(R8_q), .in9(R9_q), .in10(R10_q), .in11(R11_q), .in12(R12_q), .in13(R13_q), .in14(R14_q),
    .in15(R15_q), .out(Dataout), .sel(Rx), .en(R_W_prime));
  Hex_Digit_Display hex_digit_display_7 (.value(undriven_4));  // open: dp
  Hex_Digit_Display hex_digit_display_8 (.value(Dataout[3:0]));  // open: dp
endmodule

// ALU
module Alu (
  input  [7:0] A,
  input  [7:0] B,
  input  [3:0] SELECT,
  output [15:0] ALU_output
);

  wire adder_1_cout, subtractor_1_bout;
  wire [2:0] bit_extender_2_out;
  wire [7:0] adder_1_out, adder_2_out, and_1_out, bit_extender_1_out, bit_extender_5_out, bit_extender_6_out,
       divider_1_out, divider_1_rem, multiplier_1_cout, multiplier_1_out, not_1_out, or_1_out, shifter_1_out,
       shifter_2_out, shifter_3_out, shifter_4_out, subtractor_1_out, subtractor_2_out;
  wire [15:0] bit_extender_3_out, bit_extender_4_out, bit_extender_7_out, bit_extender_8_out,
       bit_extender_9_out, bit_extender_10_out, bit_extender_11_out, bit_extender_12_out,
       bit_extender_13_out, bit_extender_14_out, bit_extender_15_out;

  assign bit_extender_1_out = {{7{1'b0}}, 1'b1};  // Bit_Extender bit_extender_1
  Bit_Extender #(.out_width(3)) bit_extender_2 (.in(B), .out(bit_extender_2_out));
  assign bit_extender_3_out = {{8{1'b0}}, B};  // Bit_Extender bit_extender_3
  assign bit_extender_4_out = {{8{1'b0}}, A};  // Bit_Extender bit_extender_4
  Adder adder_1 (.a(A), .b(B), .out(adder_1_out), .cout(adder_1_cout));  // open: cin
  Subtractor subtractor_1 (.a(A), .b(B), .out(subtractor_1_out), .bout(subtractor_1_bout));  // open: bin
  Multiplier multiplier_1 (.a(A), .b(B), .out(multiplier_1_out), .cout(multiplier_1_cout));  // open: cin
  Divider divider_1 (.a(A), .b(B), .out(divider_1_out), .rem(divider_1_rem));  // open: upper
  Adder adder_2 (.b(bit_extender_1_out), .out(adder_2_out));  // open: a, cin, cout
  Subtractor subtractor_2 (.a(A), .b(bit_extender_1_out), .out(subtractor_2_out));  // open: bin, bout
  assign and_1_out = A & B;  // AND_Gate and_1, 8 bits wide
  assign or_1_out = A | B;  // OR_Gate or_1, 8 bits wide
  assign not_1_out = ~A;  // NOT_Gate not_1, 8 bits wide
  Shifter #(.shift("lr")) shifter_1 (.in(A), .\dist (bit_extender_2_out), .out(shifter_1_out));
  Shifter shifter_2 (.in(A), .\dist (bit_extender_2_out), .out(shifter_2_out));
  Shifter #(.shift("rr")) shifter_3 (.in(A), .\dist (bit_extender_2_out), .out(shifter_3_out));
  Shifter #(.shift("rl")) shifter_4 (.in(A), .\dist (bit_extender_2_out), .out(shifter_4_out));
  assign bit_extender_5_out = {{7{1'b0}}, adder_1_cout};  // Bit_Extender bit_extender_5
  assign bit_extender_6_out = {{7{1'b0}}, subtractor_1_bout};  // Bit_Extender bit_extender_6
  assign bit_extender_7_out = {{8{1'b0}}, adder_2_out};  // Bit_Extender bit_extender_7
  assign bit_extender_8_out = {{8{1'b0}}, subtractor_2_out};  // Bit_Extender bit_extender_8
  assign bit_extender_9_out = {{8{1'b0}}, and_1_out};  // Bit_Extender bit_extender_9
  assign bit_extender_10_out = {{8{1'b0}}, or_1_out};  // Bit_Extender bit_extender_10
  assign bit_extender_11_out = {{8{1'b0}}, not_1_out};  // Bit_Extender bit_extender_11
  assign bit_extender_12_out = {{8{1'b0}}, shifter_1_out};  // Bit_Extender bit_extender_12
  assign bit_extender_13_out = {{8{1'b0}}, shifter_2_out};  // Bit_Extender bit_extender_13
  assign bit_extender_14_out = {{8{1'b0}}, shifter_3_out};  // Bit_Extender bit_extender_14
  assign bit_extender_15_out = {{8{1'b0}}, shifter_4_out};  // Bit_Extender bit_extender_15
  Multiplexer #(.select(4), .width(16), .disabled(0)) multiplexer_1 (
    .in0(bit_extender_3_out), .in1(bit_extender_4_out), .in2({bit_extender_5_out, adder_1_out}),
    .in3({bit_extender_6_out, subtractor_1_out}), .in4({multiplier_1_cout, multiplier_1_out}),
    .in5({divider_1_rem, divider_1_out}), .in6(bit_extender_7_out), .in7(bit_extender_8_out),
    .in8(bit_extender_9_out), .in9(bit_extender_10_out), .in10(bit_extender_11_out), .in11({A, B}),
    .in12(bit_extender_12_out), .in13(bit_extender_13_out), .in14(bit_extender_14_out),
    .in15(bit_extender_15_out), .out(ALU_output), .sel(SELECT));  // open: en

  // Notes on the sheet:
  //   BitExtender
  //   Increment-----------------------------
  //   Decrement-----------------------
  //   Exchange
  //   Load
  //   Store
  //   Add
  //   Sub
  //   Mul
  //   Div
  //   And
  //   OR
  //   ShiftRight
  //   ShiftLeft
  //   Rotateright
  //   RotateLeft
  //   ALU-8bit 
  //   Not
  //   0-adder|1-sub|2-mpy|3-div|4-and|5-or|6-xnor|7-xor|8-lls|9-lrs|10-ars|11-rr|12-rl
endmodule

module pc (
  input  [7:0] PC_INput,
  input  PC_enable,
  input  Clock,
  input  PC_reset,
  output [7:0] PC_OUT
);

  wire [3:0] undriven, undriven_2;
  wire [7:0] adder_1_out;

  Hex_Digit_Display hex_digit_display_1 (.value(undriven));  // open: dp
  Hex_Digit_Display hex_digit_display_2 (.value(PC_INput[3:0]));  // open: dp
  Hex_Digit_Display hex_digit_display_3 (.value(PC_INput[7:4]));  // open: dp
  Adder adder_1 (.a(PC_INput), .b(PC_OUT), .out(adder_1_out), .cin(1'b1));  // open: cout
  Hex_Digit_Display hex_digit_display_4 (.value(PC_OUT[7:4]));  // open: dp
  Hex_Digit_Display hex_digit_display_5 (.value(undriven_2));  // open: dp
  Register register_1 (.D(adder_1_out), .en(PC_enable), .Q(PC_OUT), .clk(Clock), .clr(PC_reset));
  Hex_Digit_Display hex_digit_display_6 (.value(PC_OUT[3:0]));  // open: dp
endmodule

module PSW (
  input  [15:0] INPUT,
  input  [7:0] OP_2,
  input  [7:0] OP_1,
  output ODD_PARITY,
  output EVEN_PARITY,
  output ZERO,
  output SIGN_BIT,
  output HALF_CARRY
);

  wire [7:0] undriven, undriven_2;

  Comparator #(.width(16)) comparator_1 (.a(INPUT), .b({16{1'b0}}), .eq(ZERO));  // open: gt, lt
  Adder adder_1 (.a(undriven), .b(undriven_2), .cout(HALF_CARRY));  // open: out, cin
  xor odd_parity_1 (ODD_PARITY, INPUT[1], INPUT[2], INPUT[3], INPUT[4], INPUT[5], INPUT[6], INPUT[7], INPUT[8], INPUT[9], INPUT[10], INPUT[11], INPUT[12], INPUT[13], INPUT[14], INPUT[15], INPUT[0]);
  xnor even_parity_1 (EVEN_PARITY, INPUT[1], INPUT[2], INPUT[3], INPUT[4], INPUT[5], INPUT[6], INPUT[7], INPUT[8], INPUT[9], INPUT[10], INPUT[11], INPUT[12], INPUT[13], INPUT[14], INPUT[15], INPUT[0]);

  assign SIGN_BIT = INPUT[7];

  // Notes on the sheet:
  //   ZERO
endmodule
